# Fritzing sketch Colour Mixing Lamp Breadboard (saved by Fritzing 0.9.1b)
breadboards: 1

parts:
  Part1 = Arduino Uno (Rev3)
  LED1 = RGB LED (com. anode, rbg) [package="5 mm [THT]"]
  R1 = Resistor [tolerance=±5% resistance=220 package=THT]
  R2 = Resistor [tolerance=±5% resistance=220 package=THT]
  R3 = Resistor [tolerance=±5% resistance=220 package=THT]
  S1 = Pushbutton [package="[THT]"]
  R4 = Resistor [tolerance=±5% resistance=10k package=THT]
  C1 = Ceramic Capacitor [capacitance=0.1nF package="100 mil [THT, multilayer]"]

nets:
  N1: Part1.D9_PWM, R1.Pin_0
  N2: Part1.D10_PWM/SS, R2.Pin_0
  N3: Part1.D11_PWM/MOSI, R3.Pin_0
  N4: Part1.D2, S1.Pin_3, S1.Pin_4, R4.Pin_1, C1.1
  N5: Part1.5V, S1.Pin_1, S1.Pin_2
  N6: Part1.GND, LED1.common_anode, R4.Pin_0, C1.0
  N7: LED1.red_cathode, R1.Pin_1
  N8: LED1.blue_cathode, R2.Pin_1
  N9: LED1.green_cathode, R3.Pin_1
